# Fritzing sketch 電路圖 (saved by Fritzing 0.9.3b)
breadboards: 1

parts:
  元件1 = LinkIt 7697
  MIC1 = Microphone

nets:
  N1: 元件1.P16, 元件1.RTC_PWR_POS, MIC1.pin2
  N2: 元件1.GND, 元件1.RTC_PWR_NEG, MIC1.pin1

custom parts:
  LinkIt 7697: LinkIt 7697 is an IoT development board based on MT7697, supporting Wi-Fi and Bluetooth Low Energy connectivity.
